# Fritzing sketch team6_crkt (saved by Fritzing 0.9.3b)

parts:
  L298N1 = L298N DC motor driver
  M1 = DC Motor
  M2 = DC Motor
  Part1 = Arduino Uno (Rev3)
  L298N2 = L298N DC motor driver
  M3 = DC Motor
  M4 = DC Motor
  Part2 = Bluetooth HC-05 Macho
  BAT2 = 12 battery [package=battery]
  WeMos_D1_Mini_Relay_Shield_V1 = WeMos D1 Mini Relay Shield V2
  WATER_PUMP1 = water pump/motor

nets:
  N1: L298N1.OUT1, M2.pin_2
  N2: L298N1.OUT2, M2.pin_1
  N3: L298N1.OUT3, M1.pin_2
  N4: L298N1.OUT4, M1.pin_1
  N5: L298N1.12V, BAT2.+, WeMos_D1_Mini_Relay_Shield_V1.COM
  GND: L298N1.GND, L298N2.GND, BAT2.-, WATER_PUMP1.pin_1
  N6: Part1.A1, Part2.TXD
  N7: Part1.A2, Part2.RXD
  N8: Part1.D4, WeMos_D1_Mini_Relay_Shield_V1.D2
  5V: Part1.5V, Part2.VCC, WeMos_D1_Mini_Relay_Shield_V1.5V
  GND_2: Part1.GND, Part2.GND, WeMos_D1_Mini_Relay_Shield_V1.G
  N9: L298N2.OUT1, M4.pin_2
  N10: L298N2.OUT2, M4.pin_1
  N11: L298N2.OUT3, M3.pin_2
  N12: L298N2.OUT4, M3.pin_1

custom parts:
  L298N DC motor driver: 2x DC motor driver with 78M05 positive voltage regulator (7..35 V) L298N: max 46 V, 2 A Set 5 V Enable jumper to enable 5 V regultor (needed for the L298N) and +5 V output at screw terminal or supply external +5 V at screw terminal Set ENA and/or ENB to +5 V to enable motor permanently or supply ENA and/or ENB with PWM signal IN1 and IN2 set rotation directory for motor A (OUT1/OUT2) IN2 and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
  12 battery: 12V lead acid type battery, like the Husqvarna YTH2448 12V 35AH battery. This is the mini version 1/4 the size of the actual battery to be closer to typical breadboard parts (around 2in wide rathher than 7in). The pads in pcb are sized to accomidate up to 14ga wire (as these batterys will deliver high currents.)
  water pump/motor: WATER PUMP BY ARDUBLOCKTR
